// Logisim project B1Group3.circ as structural Verilog: 3 circuits, main circuit circuit1
module circuit1 (
  input  cs0,
  input  cs1,
  input  cs2,
  output En,
  output Cin,
  output S2,
  output S1,
  output cs1cs0
);

  wire n7404_1_p2, n7404_1_p4, n7404_1_p6, n7404_1_p9, n7408_1_p3, n7408_1_p6, n7408_1_p11, n7408_1_p14,
       n7408_2_p3;

  // _7404 7404_1: pin names not known; wires that end beside it: cs0, n7404_1_p2, cs1, n7404_1_p4, cs2, n7404_1_p6, 1'b0, 1'b1, n7404_1_p9, En
  // _7408 7408_1: pin names not known; wires that end beside it: cs1, n7404_1_p2, n7408_1_p3, cs2, n7404_1_p4, n7408_1_p6, 1'b0, 1'b1, n7404_1_p4, cs0, n7408_1_p11, cs0, n7408_1_p6, n7408_1_p14
  // _7408 7408_2: pin names not known; wires that end beside it: n7404_1_p6, cs1, n7408_2_p3, n7408_2_p3, n7404_1_p2, S2, 1'b0, 1'b1, n7404_1_p4, n7404_1_p2, S1, cs0, cs1, cs1cs0
  // _7432 7432_1: pin names not known; wires that end beside it: n7408_1_p3, n7408_1_p14, Cin, n7408_1_p11, S2, n7404_1_p9, 1'b0, 1'b1, 1'b1

  // Notes on the sheet:
  //   cs2'
  //   cs1'
  //   cs0'
  //   cs2cs1'
  //   cs2'cs1
  //   cs1cs0'
  //   cs1'cs0
  //   cs2'cs1cs0'
  //   cs2cs1'cs0
endmodule

module Main (
  input  A3,
  input  A2,
  input  A1,
  input  A0,
  input  B3,
  input  B2,
  input  B1,
  input  B0,
  input  cs2,
  input  cs1,
  input  cs0,
  output S3,
  output S2,
  output S1,
  output S0,
  output S,
  output C,
  output V,
  output Z
);

  wire circuit1_1_cin, circuit1_1_en, circuit1_1_s1, circuit1_1_s2, n7404_1_p2, n7404_1_p4, n7404_1_p6,
       n7404_1_p10, n7408_1_p2, n7432_1_p2, n7432_1_p3, n7432_1_p5, n7432_1_p6, n7432_1_p9, n7432_1_p11,
       n7432_1_p12, n7432_1_p14, n7432_2_p3, n7432_2_p6, n7432_2_p10, n7483_1_p10, n7486_1_p3, n7486_1_p6,
       n7486_1_p11, n7486_1_p14, n74157_1_p4, n74157_1_p7, n74157_1_p13, n74157_1_p16, n74157_2_p4,
       n74157_2_p7, n74157_2_p13, n74157_2_p16;

  // _7486 7486_1: pin names not known; wires that end beside it: A0, B0, n7486_1_p3, A1, B1, n7486_1_p6, 1'b0, 1'b1, B3, A3, n7486_1_p11, B2, A2, n7486_1_p14
  // _7432 7432_1: pin names not known; wires that end beside it: A0, n7432_1_p2, n7432_1_p3, A1, n7432_1_p5, n7432_1_p6, 1'b0, 1'b1, n7432_1_p9, A3, n7432_1_p11, n7432_1_p12, A2, n7432_1_p14
  // _7408 7408_1: pin names not known; wires that end beside it: B0, n7408_1_p2, n7432_1_p2, B1, n7408_1_p2, n7432_1_p5, 1'b0, 1'b1, n7408_1_p2, B3, n7432_1_p9, n7408_1_p2, B2, n7432_1_p12
  // _7404 7404_1: pin names not known; wires that end beside it: B0, n7404_1_p2, B1, n7404_1_p4, B2, n7404_1_p6, 1'b0, 1'b1, B3, n7404_1_p10
  circuit1 circuit1_1 (
    .cs0(cs0), .cs1(cs1), .cs2(cs2), .En(circuit1_1_en), .Cin(circuit1_1_cin), .S2(circuit1_1_s2),
    .S1(circuit1_1_s1), .cs1cs0(n7408_1_p2));
  // _74157 74157_1: pin names not known; wires that end beside it: circuit1_1_s1, n7432_1_p3, n7486_1_p3, n74157_1_p4, n7432_1_p6, n7486_1_p6, n74157_1_p7, 1'b0, 1'b1, 1'b0, n7432_1_p11, n7486_1_p11, n74157_1_p13, n7432_1_p14, n7486_1_p14, n74157_1_p16
  // _74157 74157_2: pin names not known; wires that end beside it: circuit1_1_s2, B0, n7404_1_p2, n74157_2_p4, B1, n7404_1_p4, n74157_2_p7, 1'b0, 1'b1, circuit1_1_en, B3, n7404_1_p10, n74157_2_p13, B2, n7404_1_p6, n74157_2_p16
  // _7483 7483_1: pin names not known; wires that end beside it: 1'b0, S2, n74157_1_p16, n74157_2_p16, 1'b1, S1, n74157_2_p7, n74157_1_p7, 1'b0, n7483_1_p10, circuit1_1_cin, 1'b0, n74157_2_p4, n74157_1_p4, S0, 1'b0
  // _7483 7483_2: pin names not known; wires that end beside it: 1'b0, 1'b0, 1'b0, 1'b1, C, 1'b0, 1'b0, 1'b0, n7483_1_p10, 1'b0, n74157_2_p13, n74157_1_p13, S
  // _7432 7432_2: pin names not known; wires that end beside it: S0, S1, n7432_2_p3, n7432_2_p3, S2, n7432_2_p6, 1'b1, S, n7432_2_p6, n7432_2_p10
  // _7486 7486_2: pin names not known; wires that end beside it: C, n7483_1_p10, C, V, 1'b1, n7432_2_p10, 1'b1, Z

  assign S3 = S;
endmodule

module test (
  input  A3,
  input  A2,
  input  A1,
  input  A0,
  input  B3,
  input  B2,
  input  B1,
  input  B0,
  input  cs2,
  input  cs1,
  input  cs0,
  output S3,
  output S2,
  output S1,
  output S0,
  output S,
  output C,
  output V,
  output Z
);

  Main main_1 (
    .A3(A3), .A2(A2), .A1(A1), .A0(A0), .B3(B3), .B2(B2), .B1(B1), .B0(B0), .cs2(cs2), .cs1(cs1), .cs0(cs0),
    .S3(S3), .S2(S2), .S1(S1), .S0(S0), .S(S), .C(C), .V(V), .Z(Z));
endmodule
