// Logisim project B1_3.circ as structural Verilog: 8 circuits, main circuit main
// FPA
module main (
  input  [15:0] Input_A,
  input  [15:0] Input_B,
  output invalid_num_1,
  output INF_1,
  output NAN_1,
  output [3:0] out_6,
  output [15:0] finalResult,
  output Overflow,
  output Underflow,
  output invalid_num_2,
  output INF_2,
  output NAN_2
);

  wire comparator_1_gt, comparator_1_lt, inputProcessing_op, normalizer_1_all_zero_detector,
       normalizer_1_underflow, normalizer_2_underflow, not_1_out, not_2_out, or_1_out, subtractor_1_bout;
  wire [3:0] inputProcessing_exp1, inputProcessing_exp2, multiplexer_1_out, multiplexer_2_out,
       normalizer_1_normedexp, normalizer_2_normedexp;
  wire [15:0] adder_1_out, inputProcessing_frac1, inputProcessing_frac2, multiplexer_3_out,
       multiplexer_4_out, multiplexer_5_out, n16bitcompwithlargesmall_1_large,
       n16bitcompwithlargesmall_1_small, normalizer_1_fraction, normalizer_2_fraction, rounder_1_roundedfrac,
       shifter_1_out, subtractor_2_out;
  wire [15:15] signbitout_1_signbit;

  input_checker input_checker_1 (.\input (Input_A), .invalid_Num(invalid_num_1), .INF(INF_1), .NAN(NAN_1));
  inputProcessing inputProcessing (
    .in_1(Input_A), .in_2(Input_B), .frac1(inputProcessing_frac1), .exp1(inputProcessing_exp1),
    .op(inputProcessing_op), .frac2(inputProcessing_frac2), .exp2(inputProcessing_exp2));
  signBitOut signbitout_1 (.X(Input_A), .Y(Input_B), .signBit(signbitout_1_signbit[15]));
  input_checker input_checker_2 (.\input (Input_B), .invalid_Num(invalid_num_2), .INF(INF_2), .NAN(NAN_2));
  Comparator #(.width(4), .mode("unsigned")) comparator_1 (
    .a(inputProcessing_exp1), .b(inputProcessing_exp2), .gt(comparator_1_gt), .lt(comparator_1_lt));  // open: eq
  Multiplexer #(.width(4), .enable("false")) multiplexer_1 (
    .in0(inputProcessing_exp1), .in1(inputProcessing_exp2), .out(multiplexer_1_out), .sel(comparator_1_lt));
  not not_1 (not_1_out, comparator_1_gt);
  Multiplexer #(.width(4), .enable("false")) multiplexer_2 (
    .in0(inputProcessing_exp2), .in1(inputProcessing_exp1), .out(multiplexer_2_out), .sel(comparator_1_lt));
  // Probe on multiplexer_1_out
  // Probe on multiplexer_2_out
  Subtractor #(.width(4)) subtractor_1 (
    .a(multiplexer_1_out), .b(multiplexer_2_out), .out(out_6), .bin(1'b0), .bout(subtractor_1_bout));
  // Probe on multiplexer_3_out
  Multiplexer #(.width(16), .enable("false")) multiplexer_3 (
    .in0(inputProcessing_frac1), .in1(inputProcessing_frac2), .out(multiplexer_3_out), .sel(comparator_1_gt));
  // Probe on subtractor_1_bout
  Multiplexer #(.width(16), .enable("false")) multiplexer_4 (
    .in0(inputProcessing_frac1), .in1(inputProcessing_frac2), .out(multiplexer_4_out), .sel(not_1_out));
  // Probe on multiplexer_4_out
  Shifter #(.width(16), .shift("lr")) shifter_1 (.in(multiplexer_3_out), .\dist (out_6), .out(shifter_1_out));
  _16bitCompWithLargeSmall u_16bitcompwithlargesmall_1 (
    .X(shifter_1_out), .Y(multiplexer_4_out), .Large(n16bitcompwithlargesmall_1_large),
    .Small(n16bitcompwithlargesmall_1_small));
  // Probe on n16bitcompwithlargesmall_1_large
  // Probe on n16bitcompwithlargesmall_1_small
  Subtractor #(.width(16)) subtractor_2 (
    .a(n16bitcompwithlargesmall_1_large), .b(n16bitcompwithlargesmall_1_small), .out(subtractor_2_out),
    .bin(1'b0));  // open: bout
  Adder #(.width(16)) adder_1 (
    .a(n16bitcompwithlargesmall_1_large), .b(n16bitcompwithlargesmall_1_small), .out(adder_1_out), .cin(1'b0));  // open: cout
  Multiplexer #(.width(16), .enable("false")) multiplexer_5 (
    .in0(adder_1_out), .in1(subtractor_2_out), .out(multiplexer_5_out), .sel(inputProcessing_op));
  // Probe on multiplexer_5_out
  normalizer normalizer_1 (
    .mantissa(multiplexer_5_out), .Exp(multiplexer_1_out),
    .all_zero_detector(normalizer_1_all_zero_detector), .fraction(normalizer_1_fraction),
    .normedExp(normalizer_1_normedexp), .UnderFlow(normalizer_1_underflow));  // open: Overflow
  // Probe on normalizer_1_all_zero_detector
  // Probe on normalizer_1_fraction
  // Probe on normalizer_1_normedexp
  rounder rounder_1 (.normedFrac(normalizer_1_fraction), .roundedFrac(rounder_1_roundedfrac));
  // Probe on rounder_1_roundedfrac
  normalizer normalizer_2 (
    .mantissa(rounder_1_roundedfrac), .Exp(normalizer_1_normedexp), .fraction(normalizer_2_fraction),
    .normedExp(normalizer_2_normedexp), .Overflow(Overflow), .UnderFlow(normalizer_2_underflow));  // open: all_zero_detector
  Multiplexer #(.width(16), .enable("false")) multiplexer_6 (
    .in0({signbitout_1_signbit[15], normalizer_2_normedexp, normalizer_2_fraction[13:3]}), .in1({16{1'b0}}),
    .out(finalResult), .sel(normalizer_1_all_zero_detector));
  not not_2 (not_2_out, normalizer_1_all_zero_detector);
  and and_1 (Underflow, not_2_out, or_1_out);
  or or_1 (or_1_out, normalizer_2_underflow, normalizer_1_underflow);
endmodule

// 16bitcmp
module _16bitCompWithLargeSmall (
  input  [15:0] X,
  input  [15:0] Y,
  output [15:0] Large,
  output [15:0] Small
);

  wire comparator_1_lt;

  Comparator #(.width(16), .mode("unsigned")) comparator_1 (.a(X), .b(Y), .lt(comparator_1_lt));  // open: gt, eq
  Multiplexer #(.width(16), .enable("false")) multiplexer_1 (.in0(X), .in1(Y), .out(Large), .sel(comparator_1_lt));
  Multiplexer #(.width(16), .enable("false")) multiplexer_2 (.in0(Y), .in1(X), .out(Small), .sel(comparator_1_lt));
endmodule

module normalizer (
  input  [15:0] mantissa,
  input  [3:0] Exp,
  output all_zero_detector,
  output [15:0] fraction,
  output [3:0] normedExp,
  output Overflow,
  output UnderFlow
);

  wire and_1_out, and_2_out, and_4_out, comparator_1_eq, nor_1_out, not_1_out, not_2_out, subtractor_2_bout;
  wire [3:0] adder_1_out, multiplexer_1_out, priority_encoder_1_out, subtractor_1_out, subtractor_2_out;
  wire [15:0] multiplexer_2_out, shifter_1_out, shifter_2_out;

  Priority_Encoder #(.select(4)) priority_encoder_1 (
    .in0(mantissa[0]), .in1(mantissa[1]), .in2(mantissa[2]), .in3(mantissa[3]), .in4(mantissa[4]),
    .in5(mantissa[5]), .in6(mantissa[6]), .in7(mantissa[7]), .in8(mantissa[8]), .in9(mantissa[9]),
    .in10(mantissa[10]), .in11(mantissa[11]), .in12(mantissa[12]), .in13(mantissa[13]), .in14(mantissa[14]),
    .in15(mantissa[15]), .out(priority_encoder_1_out), .en_out(all_zero_detector));  // open: gs, en_in
  Adder #(.width(4)) adder_1 (.a(4'b0001), .b(Exp), .out(adder_1_out));  // open: cin, cout
  // Probe on priority_encoder_1_out
  Multiplexer #(.width(4), .enable("false")) multiplexer_1 (
    .in0(priority_encoder_1_out), .in1(4'b0000), .out(multiplexer_1_out), .sel(all_zero_detector));
  Comparator #(.width(4), .mode("unsigned")) comparator_1 (
    .a(multiplexer_1_out), .b(4'b1111), .eq(comparator_1_eq));  // open: gt, lt
  Subtractor #(.width(4)) subtractor_1 (.a(4'b1110), .b(multiplexer_1_out), .out(subtractor_1_out));  // open: bin, bout
  // Probe on subtractor_1_out
  Subtractor #(.width(4)) subtractor_2 (
    .a(Exp), .b(subtractor_1_out), .out(subtractor_2_out), .bout(subtractor_2_bout));  // open: bin
  // Probe on subtractor_2_bout
  Shifter #(.width(16)) shifter_1 (.in(mantissa), .\dist (subtractor_1_out), .out(shifter_1_out));
  Shifter #(.width(16), .shift("lr")) shifter_2 (.in(mantissa), .\dist (4'b0001), .out(shifter_2_out));
  not not_1 (not_1_out, comparator_1_eq);
  and and_1 (and_1_out, not_1_out, subtractor_2_bout);
  Multiplexer #(.width(16), .enable("false")) multiplexer_2 (
    .in0(shifter_1_out), .in1(shifter_2_out), .out(multiplexer_2_out), .sel(comparator_1_eq));
  Multiplexer #(.width(4), .enable("false")) multiplexer_3 (
    .in0(subtractor_2_out), .in1(adder_1_out), .out(normedExp), .sel(comparator_1_eq));
  Multiplexer #(.width(16), .enable("false")) multiplexer_4 (
    .in0(multiplexer_2_out), .in1({16{1'b0}}), .out(fraction), .sel(all_zero_detector));
  not not_2 (not_2_out, all_zero_detector);
  and and_2 (and_2_out, normedExp[0], normedExp[1], normedExp[2], normedExp[3]);
  nor nor_1 (nor_1_out, normedExp[0], normedExp[1], normedExp[2], normedExp[3]);
  and and_3 (Overflow, not_2_out, and_2_out);
  and and_4 (and_4_out, not_2_out, nor_1_out);
  or or_1 (UnderFlow, and_4_out, and_1_out);
endmodule

module rounder (
  input  [15:0] normedFrac,
  output [15:0] roundedFrac
);

  wire and_1_out, or_1_out;

  or or_1 (or_1_out, normedFrac[0], normedFrac[1], normedFrac[3]);
  and and_1 (and_1_out, or_1_out, normedFrac[2]);
  Adder #(.width(13)) adder_1 (
    .a(normedFrac[15:3]), .b({13{1'b0}}), .out(roundedFrac[15:3]), .cin(and_1_out));  // open: cout

  assign roundedFrac[2:0] = 3'b000;
endmodule

module inputProcessing (
  input  [15:0] in_1,
  input  [15:0] in_2,
  output [15:0] frac1,
  output [3:0] exp1,
  output op,
  output [15:0] frac2,
  output [3:0] exp2
);

  wire nor_1_out, nor_2_out;

  nor nor_1 (nor_1_out, in_1[0], in_1[1], in_1[2], in_1[3], in_1[4], in_1[5], in_1[6], in_1[7], in_1[8], in_1[9], in_1[10], in_1[11], in_1[12], in_1[13], in_1[14]);
  nor nor_2 (nor_2_out, in_2[0], in_2[1], in_2[2], in_2[3], in_2[4], in_2[5], in_2[6], in_2[7], in_2[8], in_2[9], in_2[10], in_2[11], in_2[12], in_2[13], in_2[14]);
  Multiplexer #(.width(16), .enable("false")) multiplexer_1 (
    .in0({2'b01, in_1[10:0], 3'b000}), .in1({16{1'b0}}), .out(frac1), .sel(nor_1_out));
  xor xor_1 (op, in_1[15], in_2[15]);
  Multiplexer #(.width(16), .enable("false")) multiplexer_2 (
    .in0({2'b01, in_2[10:0], 3'b000}), .in1({16{1'b0}}), .out(frac2), .sel(nor_2_out));

  assign exp1 = in_1[14:11];
  assign exp2 = in_2[14:11];
endmodule

module signBitOut (
  input  [15:0] X,
  input  [15:0] Y,
  output signBit
);

  wire comparator_1_lt;

  Comparator #(.width(15), .mode("unsigned")) comparator_1 (
    .a(X[14:0]), .b(Y[14:0]), .lt(comparator_1_lt));  // open: gt, eq
  Multiplexer #(.enable("false")) multiplexer_1 (.in0(X[15]), .in1(Y[15]), .out(signBit), .sel(comparator_1_lt));
endmodule

module tester (
  input  [15:0] A,
  input  [15:0] B,
  output invalid_num_1,
  output INF_1,
  output NAN_1,
  output [15:0] Output,
  output Overflow,
  output Underflow,
  output invalid_num_2,
  output INF_2,
  output NAN_2
);

  main main_1 (
    .Input_A(A), .Input_B(B), .invalid_num_1(invalid_num_1), .INF_1(INF_1), .NAN_1(NAN_1),
    .finalResult(Output), .Overflow(Overflow), .Underflow(Underflow), .invalid_num_2(invalid_num_2),
    .INF_2(INF_2), .NAN_2(NAN_2));  // open: out_6
endmodule

module input_checker (
  input  [15:0] \input ,
  output invalid_Num,
  output INF,
  output NAN
);

  wire and_1_out, not_1_out, not_2_out, or_1_out, or_2_out;

  or or_1 (or_1_out, \input [11], \input [12], \input [13], \input [14]);
  and and_1 (and_1_out, \input [11], \input [12], \input [13], \input [14]);
  or or_2 (or_2_out, \input [10], \input [9], \input [8], \input [7], \input [6], \input [5], \input [4], \input [3], \input [2], \input [1], \input [0]);
  not not_1 (not_1_out, or_1_out);
  and and_2 (invalid_Num, or_2_out, not_1_out);
  not not_2 (not_2_out, or_2_out);
  and and_3 (NAN, or_2_out, and_1_out);
  and and_4 (INF, not_2_out, and_1_out);
endmodule
